// Logisim project frisgotchi.circ as structural Verilog: 3 circuits, main circuit main
module main (
);

  wire clock_1_out;
  wire [31:0] idle_anim_1__0, idle_anim_1_out_2, idle_anim_1_out_3, idle_anim_1_out_4, idle_anim_1_out_5,
       idle_anim_1_out_7, idle_anim_1_out_8, idle_anim_1_out_9, idle_anim_1_out_10, idle_anim_1_out_11,
       idle_anim_1_out_12, idle_anim_1_out_13, idle_anim_1_out_14, idle_anim_1_out_15, idle_anim_1_out_16,
       idle_anim_1_out_17, idle_anim_1_out_18, idle_anim_1_out_19, idle_anim_1_out_20, idle_anim_1_out_21,
       idle_anim_1_out_22, idle_anim_1_out_23, idle_anim_1_out_24, idle_anim_1_out_25, idle_anim_1_out_26,
       idle_anim_1_out_27, idle_anim_1_out_28, idle_anim_1_out_29, idle_anim_1_out_30, idle_anim_1_out_31,
       idle_anim_1_out_32, idle_anim_1_out_33, selector_1_p2, selector_1_p4, selector_1_p6, selector_1_p8,
       selector_1_p10, selector_1_p12, selector_1_p14, selector_1_p16, selector_1_p18, selector_1_p20,
       selector_1_p22, selector_1_p24, selector_1_p26, selector_1_p28, selector_1_p30, selector_1_p32,
       selector_1_p34, selector_1_p36, selector_1_p38, selector_1_p40, selector_1_p42, selector_1_p44,
       selector_1_p46, selector_1_p48, selector_1_p50, selector_1_p52, selector_1_p54, selector_1_p56,
       selector_1_p58, selector_1_p60, selector_1_p62, selector_1_p64;

  DotMatrix #(.matrixcols(32), .matrixrows(32)) dotmatrix_1 (
    .col0(selector_1_p2), .col1(selector_1_p4), .col2(selector_1_p6), .col3(selector_1_p8),
    .col4(selector_1_p10), .col5(selector_1_p12), .col6(selector_1_p14), .col7(selector_1_p16),
    .col8(selector_1_p18), .col9(selector_1_p20), .col10(selector_1_p22), .col11(selector_1_p24),
    .col12(selector_1_p26), .col13(selector_1_p28), .col14(selector_1_p30), .col15(selector_1_p32),
    .col16(selector_1_p34), .col17(selector_1_p36), .col18(selector_1_p38), .col19(selector_1_p40),
    .col20(selector_1_p42), .col21(selector_1_p44), .col22(selector_1_p46), .col23(selector_1_p48),
    .col24(selector_1_p50), .col25(selector_1_p52), .col26(selector_1_p54), .col27(selector_1_p56),
    .col28(selector_1_p58), .col29(selector_1_p60), .col30(selector_1_p62), .col31(selector_1_p64));
  Clock clock_1 (.out(clock_1_out));
  idle_anim idle_anim_1 (
    .out_2(idle_anim_1_out_2), .out_3(idle_anim_1_out_3), .out_4(idle_anim_1_out_4),
    .out_5(idle_anim_1_out_5), ._0(idle_anim_1__0), .out_7(idle_anim_1_out_7), .out_8(idle_anim_1_out_8),
    .out_9(idle_anim_1_out_9), .out_10(idle_anim_1_out_10), .out_11(idle_anim_1_out_11),
    .out_12(idle_anim_1_out_12), .out_13(idle_anim_1_out_13), .out_14(idle_anim_1_out_14),
    .out_15(idle_anim_1_out_15), .out_16(idle_anim_1_out_16), .out_17(idle_anim_1_out_17),
    .out_18(idle_anim_1_out_18), .out_19(idle_anim_1_out_19), .out_20(idle_anim_1_out_20),
    .out_21(idle_anim_1_out_21), .out_22(idle_anim_1_out_22), .out_23(idle_anim_1_out_23),
    .out_24(idle_anim_1_out_24), .out_25(idle_anim_1_out_25), .out_26(idle_anim_1_out_26),
    .out_27(idle_anim_1_out_27), .out_28(idle_anim_1_out_28), .out_29(idle_anim_1_out_29),
    .out_30(idle_anim_1_out_30), .out_31(idle_anim_1_out_31), .out_32(idle_anim_1_out_32),
    .out_33(idle_anim_1_out_33));  // open: in_1
  // selector selector_1: pin names not known; wires that end beside it: clock_1_out, selector_1_p2, idle_anim_1_out_2, selector_1_p4, idle_anim_1_out_3, selector_1_p6, idle_anim_1_out_4, selector_1_p8, idle_anim_1_out_5, selector_1_p10, idle_anim_1__0, selector_1_p12, idle_anim_1_out_7, selector_1_p14, idle_anim_1_out_8, selector_1_p16, idle_anim_1_out_9, selector_1_p18, idle_anim_1_out_10, selector_1_p20, idle_anim_1_out_11, selector_1_p22, idle_anim_1_out_12, selector_1_p24, idle_anim_1_out_13, selector_1_p26, idle_anim_1_out_14, selector_1_p28, idle_anim_1_out_15, selector_1_p30, idle_anim_1_out_16, selector_1_p32, idle_anim_1_out_17, selector_1_p34, idle_anim_1_out_18, selector_1_p36, idle_anim_1_out_19, selector_1_p38, idle_anim_1_out_20, selector_1_p40, idle_anim_1_out_21, selector_1_p42, idle_anim_1_out_22, selector_1_p44, idle_anim_1_out_23, selector_1_p46, idle_anim_1_out_24, selector_1_p48, idle_anim_1_out_25, selector_1_p50, idle_anim_1_out_26, selector_1_p52, idle_anim_1_out_27, selector_1_p54, idle_anim_1_out_28, selector_1_p56, idle_anim_1_out_29, selector_1_p58, idle_anim_1_out_30, selector_1_p60, idle_anim_1_out_31, selector_1_p62, idle_anim_1_out_32, selector_1_p64, idle_anim_1_out_33, {32{1'b1}}, {32{1'b1}}, {32{1'b1}}
endmodule

module idle_anim (
  input  in_1,
  output [31:0] out_2,
  output [31:0] out_3,
  output [31:0] out_4,
  output [31:0] out_5,
  output [31:0] _0,
  output [31:0] out_7,
  output [31:0] out_8,
  output [31:0] out_9,
  output [31:0] out_10,
  output [31:0] out_11,
  output [31:0] out_12,
  output [31:0] out_13,
  output [31:0] out_14,
  output [31:0] out_15,
  output [31:0] out_16,
  output [31:0] out_17,
  output [31:0] out_18,
  output [31:0] out_19,
  output [31:0] out_20,
  output [31:0] out_21,
  output [31:0] out_22,
  output [31:0] out_23,
  output [31:0] out_24,
  output [31:0] out_25,
  output [31:0] out_26,
  output [31:0] out_27,
  output [31:0] out_28,
  output [31:0] out_29,
  output [31:0] out_30,
  output [31:0] out_31,
  output [31:0] out_32,
  output [31:0] out_33
);


  assign _0 = {32{1'b0}};
  assign out_2 = {32{1'b0}};
  assign out_3 = {32{1'b0}};
  assign out_4 = {32{1'b0}};
  assign out_5 = {32{1'b0}};
  assign out_7 = {32{1'b0}};
  assign out_8 = {32{1'b0}};
  assign out_9 = 32'h1e000;
  assign out_10 = 32'h61000;
  assign out_11 = 32'h1c80800;
  assign out_12 = 32'h2380800;
  assign out_13 = 32'h208c880;
  assign out_14 = 32'h1900740;
  assign out_15 = 32'h600040;
  assign out_16 = 32'h1880040;
  assign out_17 = 32'h2080180;
  assign out_18 = 32'h2160240;
  assign out_19 = 32'h1e10040;
  assign out_20 = 32'h10040;
  assign out_21 = 32'h10080;
  assign out_22 = 32'h8040;
  assign out_23 = 32'h8180;
  assign out_24 = 32'h8040;
  assign out_25 = 32'h8040;
  assign out_26 = 32'h4080;
  assign out_27 = 32'h3f00;
  assign out_28 = {32{1'b0}};
  assign out_29 = {32{1'b0}};
  assign out_30 = {32{1'b0}};
  assign out_31 = {32{1'b0}};
  assign out_32 = {32{1'b0}};
  assign out_33 = {32{1'b0}};
endmodule

module selector (
  input  in_1,
  input  [31:0] in_2,
  input  [31:0] in_3,
  input  [31:0] in_4,
  input  [31:0] in_5,
  input  [31:0] in_6,
  input  [31:0] in_7,
  input  [31:0] in_8,
  input  [31:0] in_9,
  input  [31:0] in_10,
  input  [31:0] in_11,
  input  [31:0] in_12,
  input  [31:0] in_13,
  input  [31:0] in_14,
  input  [31:0] in_15,
  input  [31:0] in_16,
  input  [31:0] in_17,
  input  [31:0] in_18,
  input  [31:0] in_19,
  input  [31:0] in_20,
  input  [31:0] in_21,
  input  [31:0] in_22,
  input  [31:0] in_23,
  input  [31:0] in_24,
  input  [31:0] in_25,
  input  [31:0] in_26,
  input  [31:0] in_27,
  input  [31:0] in_28,
  input  [31:0] in_29,
  input  [31:0] in_30,
  input  [31:0] in_31,
  input  [31:0] in_32,
  input  [31:0] in_33,
  input  [31:0] in_34,
  input  [31:0] in_35,
  input  [31:0] in_36,
  input  [31:0] in_37,
  input  [31:0] in_38,
  input  [31:0] in_39,
  input  [31:0] in_40,
  input  [31:0] in_41,
  input  [31:0] in_42,
  input  [31:0] in_43,
  input  [31:0] in_44,
  input  [31:0] in_45,
  input  [31:0] in_46,
  input  [31:0] in_47,
  input  [31:0] in_48,
  input  [31:0] in_49,
  input  [31:0] in_50,
  input  [31:0] in_51,
  input  [31:0] in_52,
  input  [31:0] in_53,
  input  [31:0] in_54,
  input  [31:0] in_55,
  input  [31:0] in_56,
  input  [31:0] in_57,
  input  [31:0] in_58,
  input  [31:0] in_59,
  input  [31:0] in_60,
  input  [31:0] in_61,
  input  [31:0] in_62,
  input  [31:0] in_63,
  input  [31:0] in_64,
  input  [31:0] in_65,
  output [31:0] out_66,
  output [31:0] out_67,
  output [31:0] out_68,
  output [31:0] out_69,
  output [31:0] out_70,
  output [31:0] out_71,
  output [31:0] out_72,
  output [31:0] out_73,
  output [31:0] out_74,
  output [31:0] out_75,
  output [31:0] out_76,
  output [31:0] out_77,
  output [31:0] out_78,
  output [31:0] out_79,
  output [31:0] out_80,
  output [31:0] out_81,
  output [31:0] out_82,
  output [31:0] out_83,
  output [31:0] out_84,
  output [31:0] out_85,
  output [31:0] out_86,
  output [31:0] out_87,
  output [31:0] out_88,
  output [31:0] out_89,
  output [31:0] out_90,
  output [31:0] out_91,
  output [31:0] out_92,
  output [31:0] out_93,
  output [31:0] out_94,
  output [31:0] out_95,
  output [31:0] out_96,
  output [31:0] out_97
);

  Multiplexer #(.width(32)) multiplexer_1 (.in0(in_2), .in1(in_34), .out(out_66), .sel(in_1));  // open: en
  Multiplexer #(.width(32)) multiplexer_2 (.in0(in_3), .in1(in_35), .out(out_67), .sel(in_1));  // open: en
  Multiplexer #(.width(32)) multiplexer_3 (.in0(in_5), .in1(in_37), .out(out_69), .sel(in_1));  // open: en
  Multiplexer #(.width(32)) multiplexer_4 (.in0(in_4), .in1(in_36), .out(out_68), .sel(in_1));  // open: en
  Multiplexer #(.width(32)) multiplexer_5 (.in0(in_6), .in1(in_38), .out(out_70), .sel(in_1));  // open: en
  Multiplexer #(.width(32)) multiplexer_6 (.in0(in_7), .in1(in_39), .out(out_71), .sel(in_1));  // open: en
  Multiplexer #(.width(32)) multiplexer_7 (.in0(in_8), .in1(in_40), .out(out_72), .sel(in_1));  // open: en
  Multiplexer #(.width(32)) multiplexer_8 (.in0(in_9), .in1(in_41), .out(out_73), .sel(in_1));  // open: en
  Multiplexer #(.width(32)) multiplexer_9 (.in0(in_10), .in1(in_42), .out(out_74), .sel(in_1));  // open: en
  Multiplexer #(.width(32)) multiplexer_10 (.in0(in_11), .in1(in_43), .out(out_75), .sel(in_1));  // open: en
  Multiplexer #(.width(32)) multiplexer_11 (.in0(in_13), .in1(in_45), .out(out_77), .sel(in_1));  // open: en
  Multiplexer #(.width(32)) multiplexer_12 (.in0(in_12), .in1(in_44), .out(out_76), .sel(in_1));  // open: en
  Multiplexer #(.width(32)) multiplexer_13 (.in0(in_14), .in1(in_46), .out(out_78), .sel(in_1));  // open: en
  Multiplexer #(.width(32)) multiplexer_14 (.in0(in_15), .in1(in_47), .out(out_79), .sel(in_1));  // open: en
  Multiplexer #(.width(32)) multiplexer_15 (.in0(in_16), .in1(in_48), .out(out_80), .sel(in_1));  // open: en
  Multiplexer #(.width(32)) multiplexer_16 (.in0(in_17), .in1(in_49), .out(out_81), .sel(in_1));  // open: en
  Multiplexer #(.width(32)) multiplexer_17 (.in0(in_18), .in1(in_50), .out(out_82), .sel(in_1));  // open: en
  Multiplexer #(.width(32)) multiplexer_18 (.in0(in_19), .in1(in_51), .out(out_83), .sel(in_1));  // open: en
  Multiplexer #(.width(32)) multiplexer_19 (.in0(in_21), .in1(in_53), .out(out_85), .sel(in_1));  // open: en
  Multiplexer #(.width(32)) multiplexer_20 (.in0(in_20), .in1(in_52), .out(out_84), .sel(in_1));  // open: en
  Multiplexer #(.width(32)) multiplexer_21 (.in0(in_22), .in1(in_54), .out(out_86), .sel(in_1));  // open: en
  Multiplexer #(.width(32)) multiplexer_22 (.in0(in_23), .in1(in_55), .out(out_87), .sel(in_1));  // open: en
  Multiplexer #(.width(32)) multiplexer_23 (.in0(in_24), .in1(in_56), .out(out_88), .sel(in_1));  // open: en
  Multiplexer #(.width(32)) multiplexer_24 (.in0(in_26), .in1(in_58), .out(out_90), .sel(in_1));  // open: en
  Multiplexer #(.width(32)) multiplexer_25 (.in0(in_25), .in1(in_57), .out(out_89), .sel(in_1));  // open: en
  Multiplexer #(.width(32)) multiplexer_26 (.in0(in_27), .in1(in_59), .out(out_91), .sel(in_1));  // open: en
  Multiplexer #(.width(32)) multiplexer_27 (.in0(in_28), .in1(in_60), .out(out_92), .sel(in_1));  // open: en
  Multiplexer #(.width(32)) multiplexer_28 (.in0(in_29), .in1(in_61), .out(out_93), .sel(in_1));  // open: en
  Multiplexer #(.width(32)) multiplexer_29 (.in0(in_30), .in1(in_62), .out(out_94), .sel(in_1));  // open: en
  Multiplexer #(.width(32)) multiplexer_30 (.in0(in_32), .in1(in_64), .out(out_96), .sel(in_1));  // open: en
  Multiplexer #(.width(32)) multiplexer_31 (.in0(in_31), .in1(in_63), .out(out_95), .sel(in_1));  // open: en
  Multiplexer #(.width(32)) multiplexer_32 (.in0(in_33), .in1(in_65), .out(out_97), .sel(in_1));  // open: en
endmodule
